# Fritzing sketch mastermind_neotrellis (saved by Fritzing 0.9.3b)
breadboards: 1

parts:
  Part1 = Arduino Mega 2560 (Rev3)
  Part2 = Adafruit NeoTrellis 4x4 [part_number=https://www.adafruit.com/product/3954]
  Part3 = Adafruit NeoTrellis 4x4 [part_number=https://www.adafruit.com/product/3954]
  Part4 = Adafruit NeoTrellis 4x4 [part_number=https://www.adafruit.com/product/3954]
  Part5 = Adafruit NeoTrellis 4x4 [part_number=https://www.adafruit.com/product/3954]
  S1 = Pushbutton [package="[THT]"]
  S2 = Pushbutton [package="[THT]"]

nets:
  N1: Part1.A2, Part2.INT, Part3.INT, Part4.INT, Part5.INT
  N2: Part1.D21/SCL, Part2.SCL, Part3.SCL, Part4.SCL, Part5.SCL
  N3: Part1.D20/SDA, Part1.SDA, Part2.SDA, Part3.SDA, Part4.SDA, Part5.SDA
  VIN: Part1.5V, Part2.VIN, Part3.VIN, Part4.VIN, Part5.VIN
  GND: Part1.GND, Part2.GND, Part3.GND, Part4.GND, Part5.GND, S1.Pin_3, S1.Pin_4, S2.Pin_3, S2.Pin_4
  N4: Part1.D2_PWM, S2.Pin_1, S2.Pin_2
  N5: Part1.D3_PWM, S1.Pin_1, S1.Pin_2
